# Fritzing sketch Smart Alarm (saved by Fritzing 1.0.4)
breadboards: 1

parts:
  J1 = STM32 Nucleo boards
  OLED_I2C1 = OLED 128x64 I2C Monochrome Display
  A1 = Wemos S2 Mini [part_number="WeMos D1 Mini Lite"]
  Keypad4x2 = Keypad Membran 4x4  # not connected
  S1 = SWITCH-MOMENTARY-2 [package=reed_switch_pth]  # not connected

nets:
  3V3: J1.3V3, OLED_I2C1.VDD
  N1: J1.5V, A1.Pin_17
  N2: J1.GND#1188, OLED_I2C1.GND
  N3: J1.GND#1189, A1.Pin_18
  N4: J1.PC9, OLED_I2C1.SCK
  N5: J1.PB8, OLED_I2C1.SDA

custom parts:
  Wemos S2 Mini: A mini wifi board based on the ESP32-S2FN4R2.
  Keypad Membran 4x4: Membrane Keypad 4x4 Matrix
